# Fritzing sketch LEDviaApp_Micro (saved by Fritzing 0.9.3b)
breadboards: 1

parts:
  R2 = Resistor [tolerance=±5% resistance=10k package=THT]
  R3 = Resistor [tolerance=±5% resistance=22k package=THT]
  U1 = mystery part, 4 pins [chip_label=Bluetooth part_number=HC-06]
  U2 = mystery part, 3 pins [chip_label=LED-Stripe part_number=LED-Stripe]
  C1 = Electrolytic Capacitor [capacitance=1mF voltage=16V package="100 mil [THT, electrolytic]"]
  Power_plug = Power plug [part_number="5 VDC / 10 A"]
  Bauteil1 = Arduino Micro (Rev3)
  R4 = Resistor [tolerance=±5% resistance=330 package=THT]

nets:
  N1: R2.Pin_0, Bauteil1.D1/TX
  N2: R2.Pin_1, R3.Pin_0, U1.pin1
  GND: R3.Pin_1, U1.pin3, U2.pin1, C1.-, Power_plug.GND, Bauteil1.GND
  N3: U1.pin2, Bauteil1.D0/RX
  VCC: U1.pin4, U2.pin2, C1.+, Power_plug.VCC, Bauteil1.5V
  N4: U2.pin3, R4.Pin_0
  N5: Bauteil1.MOSI, R4.Pin_1
