# Fritzing sketch LEDviaApp (saved by Fritzing 0.9.3b)
breadboards: 1

parts:
  Q1 = NPN-Transistor [part_number=BC574B package="TO92 [THT]"]
  R2 = Resistor [tolerance=±5% resistance=10k package=THT]
  R3 = Resistor [tolerance=±5% resistance=22k package=THT]
  U1 = mystery part, 4 pins [chip_label=Bluetooth part_number=HC-06]
  U2 = mystery part, 3 pins [chip_label=LED-Stripe part_number=LED-Stripe]
  C1 = Electrolytic Capacitor [capacitance=1mF voltage=16V package="100 mil [THT, electrolytic]"]
  Power_plug = Power plug [part_number="5 VDC / 10 A"]
  Arduino_UNO_(Rev_3) = Arduino Uno (Rev3)
  R5 = Resistor [tolerance=±5% resistance=220 package=THT]
  R6 = Resistor [tolerance=±5% resistance=220 package=THT]
  LED1 = LED - 5mm [color="Red (633nm)" package="5 mm [THT]"]

nets:
  N1: Q1.E, U1.pin4
  N2: Q1.B, Arduino_UNO_(Rev_3).D4
  VCC: Q1.C, U2.pin2, C1.+, Power_plug.VCC, Arduino_UNO_(Rev_3).VIN
  N3: R2.Pin_0, Arduino_UNO_(Rev_3).D1/TX
  N4: R2.Pin_1, R3.Pin_0, U1.pin1
  GND: R3.Pin_1, U1.pin3, U2.pin1, C1.-, Power_plug.GND, Arduino_UNO_(Rev_3).GND, LED1.cathode
  N5: U1.pin2, Arduino_UNO_(Rev_3).D0/RX
  N6: U2.pin3, R6.Pin_0
  N7: Arduino_UNO_(Rev_3).D11_PWM/MOSI, R6.Pin_1
  N8: Arduino_UNO_(Rev_3).D7, R5.Pin_1
  N9: R5.Pin_0, LED1.anode
